# Fritzing sketch LEDTreppe (saved by Fritzing 0.9.3b)
breadboards: 1
stripboards: 1

parts:
  Bauteil1 = Arduino Uno (Rev3)
  NEOPIXEL1 = Neopixel Strip -- Black (60/m)
  5V = Power plug
  R1 = Resistor [tolerance=±5% resistance=740 package=THT]
  C1 = Electrolytic Capacitor [capacitance=1mF voltage=10V package="200 mil [THT, electrolytic]"]
  IR1 = TSOP312.., 314.. [package=THT]
  (TODO!) = Resistor [tolerance=±5% resistance=220 package=THT]
  (TODO!)_2 = Resistor [tolerance=±5% resistance=220 package=THT]
  D1 = LTE-302 [package=lte-302]  # not connected

nets:
  GND: Bauteil1.GND, NEOPIXEL1.GND, 5V.GND, C1.-, IR1.GND, (TODO!).Pin_1
  N1: Bauteil1.D2, IR1.Data
  N2: Bauteil1.D6_PWM, R1.Pin_0
  VIN: Bauteil1.VIN, NEOPIXEL1.DI, 5V.VCC, C1.+, (TODO!)_2.Pin_1
  N3: NEOPIXEL1.+5V, R1.Pin_1

custom parts:
  Neopixel Strip -- Black (60/m): Neopixel Strip, Black, 60 pixels per meter.
